# Fritzing sketch moisture-sensor (saved by Fritzing 0.9.2b)
breadboards: 1

parts:
  Part1 = Arduino Uno (Rev3) - ICSP
  LED1 = RGB LED (com. cathode, rbg) [package="5 mm [THT]"]
  R1 = Resistor [tolerance=±5% resistance=220 package=THT]
  R2 = Resistor [tolerance=±5% resistance=10k package=THT]
  R3 = Resistor [tolerance=±5% resistance=220 package=THT]
  U1 = POT [package=alps_pot]
  LCD1 = LCD screen  # not connected
  S1 = Pushbutton [package="[THT]"]

nets:
  N1: Part1.D8, R1.Pin_0
  N2: Part1.D9_PWM, R2.Pin_0
  N3: Part1.D10_PWM/SS, R3.Pin_0
  N4: Part1.D2, S1.Pin_3, S1.Pin_4
  N5: Part1.GND, U1.S, S1.Pin_1, S1.Pin_2
  N6: LED1.red_anode, R1.Pin_1
  N7: LED1.common_cathode, U1.A
  N8: LED1.blue_anode, R2.Pin_1
  N9: LED1.green_anode, R3.Pin_1

notes:
  LCM1602 controller on display
  GND
  Vcc
  SDA
  SCL
  Moisture sensor with HL-01
  A0
  D0
  GND
  VCC
